# Fritzing sketch Sketch (saved by Fritzing 0.9.2b)
breadboards: 1

parts:
  part = ESP8266-12 [part_number=ESP8266-12]
  R1 = Resistor [tolerance=±5% resistance=10k package=THT]
  R2 = Resistor [tolerance=±5% resistance=10k package=THT]
  R3 = Resistor [tolerance=±5% resistance=10k package=THT]
  R4 = Resistor [tolerance=±5% resistance=470 package=THT]
  J1 = male pin header, 3 pins [form="♂ (male)"]
  J2 = male pin header, 3 pins [form="♂ (male)"]

nets:
  N1: part.REST, R1.Pin_1, R4.Pin_0
  N2: part.CH_PD, R2.Pin_1
  N3: part.GPIO16, R4.Pin_1
  N4: part.VCC, R1.Pin_0, R2.Pin_0
  N5: part.TXD, J1.pin1
  N6: part.RXD, J1.pin2
  N7: part.GPIO2, J2.pin2
  N8: part.GPIO15, R3.Pin_0
  N9: part.GND, J1.pin3, J2.pin3
  N10: R3.Pin_1, J2.pin1
